// Logisim project proje.circ as structural Verilog: 6 circuits, main circuit anadevre
module anadevre (
  input  [3:0] in_1,
  input  reset,
  output E
);

  wire and_1_out, Clk_out, controlunit_1_p4, controlunit_1_p5, controlunit_1_p11, not_1_out;
  wire [1:0] controlunit_1_p3, controlunit_1_p8, controlunit_1_p10;
  wire [2:0] controlunit_1_p6, controlunit_1_p7;
  wire [3:0] AC_output, alu4bit_1_output_ac, AR_output, controlled_buffer_1_out, controlunit_1_p1,
       controlunit_1_p9, DR_output, IR_output_0__3, OUTR_output, PC_output;
  wire [6:0] controlunit_1_p12;
  wire [7:0] controlled_buffer_2_out, ram_1_data;

  not not_1 (not_1_out, controlunit_1_p4);
  and and_1 (and_1_out, not_1_out, Clk_out);
  // ControlUnit controlunit_1: pin names not known; wires that end beside it: controlunit_1_p1, and_1_out, controlunit_1_p3, controlunit_1_p4, controlunit_1_p5, controlunit_1_p6, controlunit_1_p7, controlunit_1_p8, controlunit_1_p9, controlunit_1_p10, controlunit_1_p11, controlunit_1_p12
  Clock Clk (.out(Clk_out));
  RAM #(.addrWidth(4), .bus("separate")) ram_1 (
    .addr(AR_output), .din(controlled_buffer_2_out), .data(ram_1_data), .str(controlunit_1_p3[0]),
    .clk(and_1_out), .clr(reset));  // open: sel, ld
  ALU4Bit alu4bit_1 (
    .AC(AC_output), .DR(controlled_buffer_1_out), .INPR(in_1), .AND(controlunit_1_p12[0]),
    .ADD(controlunit_1_p12[1]), .CMA(controlunit_1_p12[2]), .LD_DR(controlunit_1_p12[3]),
    .LD_INPR(controlunit_1_p12[4]), .CIR(controlunit_1_p12[5]), .CIL(controlunit_1_p12[6]), .CLK(and_1_out),
    .CLR(controlunit_1_p5), .output_AC(alu4bit_1_output_ac), .E_output(E));
  Register4Bit AR (
    .INPUT(controlled_buffer_2_out[3:0]), .CLK(and_1_out), .LD(controlunit_1_p6[0]),
    .INC(controlunit_1_p6[1]), .CLR(reset), .OUTPUT(AR_output));
  // Probe on PC_output
  Register4Bit PC (
    .INPUT(controlled_buffer_2_out[3:0]), .CLK(and_1_out), .LD(controlunit_1_p7[0]),
    .INC(controlunit_1_p7[1]), .CLR(reset), .OUTPUT(PC_output));
  Register4Bit DR (
    .INPUT(controlled_buffer_2_out[3:0]), .CLK(and_1_out), .LD(controlunit_1_p8[0]), .CLR(reset),
    .OUTPUT(DR_output));  // open: INC
  Register4Bit AC (
    .INPUT(alu4bit_1_output_ac), .CLK(and_1_out), .LD(controlunit_1_p9[1]), .INC(controlunit_1_p9[2]),
    .CLR(controlunit_1_p9[3]), .OUTPUT(AC_output));
  Register8Bit_IR IR (
    .Input(controlled_buffer_2_out), .CLK(and_1_out), .LD(controlunit_1_p10[0]),
    .Output_0__3(IR_output_0__3), .Output_4__7(controlunit_1_p1));
  Register4Bit OUTR (
    .INPUT(controlled_buffer_2_out[3:0]), .CLK(and_1_out), .LD(controlunit_1_p11), .CLR(reset),
    .OUTPUT(OUTR_output));  // open: INC
  // Probe on AR_output
  // Probe on DR_output
  // Probe on AC_output
  // Probe on IR_output_0__3
  // Probe on controlunit_1_p1
  // Probe on OUTR_output
  assign controlled_buffer_1_out = controlunit_1_p8[1] ? DR_output : 4'bz;  // Controlled_Buffer controlled_buffer_1
  assign controlled_buffer_2_out = controlunit_1_p3[1] ? ram_1_data : 8'bz;  // Controlled_Buffer controlled_buffer_2
  assign controlled_buffer_2_out = controlunit_1_p6[2] ? {4'b0000, AR_output} : 8'bz;  // Controlled_Buffer controlled_buffer_3
  assign controlled_buffer_2_out = controlunit_1_p7[2] ? {4'b0000, PC_output} : 8'bz;  // Controlled_Buffer controlled_buffer_4
  assign controlled_buffer_2_out = controlunit_1_p9[0] ? {4'b0000, AC_output} : 8'bz;  // Controlled_Buffer controlled_buffer_5
  assign controlled_buffer_2_out = controlunit_1_p10[1] ? {controlunit_1_p1, IR_output_0__3} : 8'bz;  // Controlled_Buffer controlled_buffer_6
endmodule

// AC
module ALU1Bit (
  input  INPR,
  input  DR,
  input  AC,
  input  AND,
  input  ADD,
  input  cin,
  input  CMA,
  input  LD_DR,
  input  LD_INPR,
  input  CIR,
  input  CIL,
  input  AC_i_1,
  input  AC_i_1_2,
  output cout,
  output output_AC
);

  wire add_out, adder_1_out, and_out, comp_out, Id_DR_out, Id_INPR_out, not_1_out, shl_out, shr_out;

  Adder #(.width(1)) adder_1 (.a(AC), .b(DR), .out(adder_1_out), .cin(cin), .cout(cout));
  not not_1 (not_1_out, AC);
  and u_and (and_out, AND, AC, DR);
  and u_add (add_out, ADD, adder_1_out);
  and comp (comp_out, CMA, not_1_out);
  and Id_DR (Id_DR_out, LD_DR, DR);
  and Id_INPR (Id_INPR_out, LD_INPR, INPR);
  and shr (shr_out, CIR, AC_i_1_2);
  and shl (shl_out, CIL, AC_i_1);
  or or_1 (output_AC, and_out, add_out, comp_out, Id_DR_out, Id_INPR_out, shr_out, shl_out);
endmodule

module ALU4Bit (
  input  [3:0] AC,
  input  [3:0] DR,
  input  [3:0] INPR,
  input  AND,
  input  ADD,
  input  CMA,
  input  LD_DR,
  input  LD_INPR,
  input  CIR,
  input  CIL,
  input  CLK,
  input  CLR,
  output [3:0] output_AC,
  output E_output
);

  wire alu1bit_1_cout, alu1bit_2_cout, alu1bit_3_cout, alu1bit_4_cout, elde_1_ac_0__ac_i_1, elde_1_ac_0__cin,
       elde_1_ac_3__ac_i_1;

  ALU1Bit alu1bit_1 (
    .AND(AND), .ADD(ADD), .CMA(CMA), .LD_DR(LD_DR), .LD_INPR(LD_INPR), .CIR(CIR), .CIL(CIL),
    .AC_i_1(elde_1_ac_0__ac_i_1), .AC_i_1_2(AC[1]), .INPR(INPR[0]), .DR(DR[0]), .AC(AC[0]),
    .cin(elde_1_ac_0__cin), .cout(alu1bit_1_cout), .output_AC(output_AC[0]));
  ALU1Bit alu1bit_2 (
    .AND(AND), .ADD(ADD), .CMA(CMA), .LD_DR(LD_DR), .LD_INPR(LD_INPR), .CIR(CIR), .CIL(CIL), .AC_i_1(AC[0]),
    .AC_i_1_2(AC[2]), .INPR(INPR[1]), .DR(DR[1]), .AC(AC[1]), .cin(alu1bit_1_cout), .cout(alu1bit_2_cout),
    .output_AC(output_AC[1]));
  ALU1Bit alu1bit_3 (
    .AND(AND), .ADD(ADD), .CMA(CMA), .LD_DR(LD_DR), .LD_INPR(LD_INPR), .CIR(CIR), .CIL(CIL), .AC_i_1(AC[1]),
    .AC_i_1_2(AC[3]), .INPR(INPR[2]), .DR(DR[2]), .AC(AC[2]), .cin(alu1bit_2_cout), .cout(alu1bit_3_cout),
    .output_AC(output_AC[2]));
  ALU1Bit alu1bit_4 (
    .AND(AND), .ADD(ADD), .CMA(CMA), .LD_DR(LD_DR), .LD_INPR(LD_INPR), .CIR(CIR), .CIL(CIL), .AC_i_1(AC[2]),
    .AC_i_1_2(elde_1_ac_3__ac_i_1), .INPR(INPR[3]), .DR(DR[3]), .AC(AC[3]), .cin(alu1bit_3_cout),
    .cout(alu1bit_4_cout), .output_AC(output_AC[3]));
  elde elde_1 (
    .AC_3__cout(alu1bit_4_cout), .AC_3__output(output_AC[3]), .AC_0_output(output_AC[0]), .CIL(CIL),
    .CIR(CIR), .ADD(ADD), .CLK(CLK), .CLR(CLR), .output_E(E_output), .AC_0__ac_i_1(elde_1_ac_0__ac_i_1),
    .AC_3__ac_i_1(elde_1_ac_3__ac_i_1), .AC_0__cin(elde_1_ac_0__cin));
endmodule

// reg
module Register4Bit (
  input  INC,
  input  LD,
  input  [3:0] INPUT,
  input  CLR,
  input  CLK,
  output [3:0] OUTPUT
);

  wire and_1_out, and_2_out, and_3_out, and_4_out, and_5_out, and_6_out, and_7_out, and_8_out, and_9_out,
       and_10_out, and_11_out, and_12_out, not_1_out, not_2_out, not_3_out, not_4_out, not_5_out, or_1_out,
       or_2_out, or_3_out, or_4_out, or_5_out, or_6_out, or_7_out, or_8_out;

  and and_1 (and_1_out, INC, not_1_out);
  not not_1 (not_1_out, LD);
  not not_2 (not_2_out, INPUT[0]);
  not not_3 (not_3_out, INPUT[1]);
  not not_4 (not_4_out, INPUT[2]);
  not not_5 (not_5_out, INPUT[3]);
  and and_2 (and_2_out, LD, INPUT[0]);
  and and_3 (and_3_out, LD, not_2_out);
  and and_4 (and_4_out, LD, INPUT[1]);
  and and_5 (and_5_out, LD, not_3_out);
  and and_6 (and_6_out, LD, INPUT[2]);
  and and_7 (and_7_out, LD, not_4_out);
  and and_8 (and_8_out, LD, INPUT[3]);
  and and_9 (and_9_out, LD, not_5_out);
  and and_10 (and_10_out, and_1_out, OUTPUT[0]);
  and and_11 (and_11_out, and_1_out, OUTPUT[0], OUTPUT[1]);
  and and_12 (and_12_out, and_1_out, OUTPUT[0], OUTPUT[1], OUTPUT[2]);
  or or_1 (or_1_out, and_2_out, and_1_out);
  or or_2 (or_2_out, and_3_out, and_1_out);
  or or_3 (or_3_out, and_4_out, and_10_out);
  or or_4 (or_4_out, and_10_out, and_5_out);
  or or_5 (or_5_out, and_6_out, and_11_out);
  or or_6 (or_6_out, and_11_out, and_7_out);
  or or_7 (or_7_out, and_8_out, and_12_out);
  or or_8 (or_8_out, and_12_out, and_9_out);
  J_K_Flip_Flop j_k_ff_1 (.J(or_1_out), .clk(CLK), .K(or_2_out), .Q(OUTPUT[0]), .reset(CLR));  // open: Qn, preset, en
  J_K_Flip_Flop j_k_ff_2 (.J(or_3_out), .clk(CLK), .K(or_4_out), .Q(OUTPUT[1]), .reset(CLR));  // open: Qn, preset, en
  J_K_Flip_Flop j_k_ff_3 (.J(or_5_out), .clk(CLK), .K(or_6_out), .Q(OUTPUT[2]), .reset(CLR));  // open: Qn, preset, en
  J_K_Flip_Flop j_k_ff_4 (.J(or_7_out), .clk(CLK), .K(or_8_out), .Q(OUTPUT[3]), .reset(CLR));  // open: Qn, preset, en
endmodule

// IR
module Register8Bit_IR (
  input  [7:0] Input,
  input  CLK,
  input  LD,
  output [3:0] Output_0__3,
  output [3:0] Output_4__7
);

  Register4Bit register4bit_1 (.INPUT(Input[3:0]), .CLK(CLK), .LD(LD), .OUTPUT(Output_0__3));  // open: INC, CLR
  Register4Bit register4bit_2 (.INPUT(Input[7:4]), .CLK(CLK), .LD(LD), .OUTPUT(Output_4__7));  // open: INC, CLR
endmodule

// E
module elde (
  input  AC_3__cout,
  input  AC_3__output,
  input  AC_0_output,
  input  CIL,
  input  CIR,
  input  ADD,
  input  CLK,
  input  CLR,
  output output_E,
  output AC_0__ac_i_1,
  output AC_3__ac_i_1,
  output AC_0__cin
);

  wire and_1_out, and_2_out, and_3_out, and_4_out, and_5_out, d_ff_1_q, not_1_out, or_1_out, or_2_out;

  and and_1 (and_1_out, AC_3__cout, ADD);
  and and_2 (and_2_out, AC_0_output, CIR);
  and and_3 (and_3_out, AC_3__output, CIL);
  or or_1 (or_1_out, AC_3__cout, AC_3__output, AC_0_output);
  or or_2 (or_2_out, and_1_out, and_2_out, and_3_out);
  not not_1 (not_1_out, or_2_out);
  and and_4 (and_4_out, or_2_out, or_1_out);
  and and_5 (and_5_out, or_1_out, not_1_out);
  D_Flip_Flop d_ff_1 (.clk(CLK), .D(output_E), .Q(d_ff_1_q), .reset(CLR));  // open: Qn, preset, en
  J_K_Flip_Flop j_k_ff_1 (.J(and_4_out), .clk(CLK), .K(and_5_out), .Q(output_E), .reset(CLR));  // open: Qn, preset, en
  and and_6 (AC_0__ac_i_1, CIL, d_ff_1_q);
  and and_7 (AC_3__ac_i_1, CIR, d_ff_1_q);
  and and_8 (AC_0__cin, ADD, d_ff_1_q);
endmodule
